# Fritzing sketch circuit_plan (saved by Fritzing 0.9.3b)
breadboards: 2
stripboards: 1

parts:
  ArduinoMicro = Arduino Micro (Rev3)
  R1 = Resistor [tolerance=±5% resistance=1k package=THT]
  LED1 = LED - 5mm [color="Red (633nm)" package="5 mm [THT]"]
  SW-KB-DISABLE = Toggle Switch [package=THT]
  R2 = Resistor [tolerance=±5% resistance=220 package=THT]
  OnethruFour-1 = Square Pushbutton
  OnethruFour-2 = Square Pushbutton
  OnethruFour-3 = Square Pushbutton
  OnethruFour-4 = Square Pushbutton
  R3 = Resistor [tolerance=±5% resistance=2.2k package=THT]
  R4 = Resistor [tolerance=±5% resistance=330 package=THT]
  R5 = Resistor [tolerance=±5% resistance=680 package=THT]
  R6 = Resistor [tolerance=±5% resistance=1k package=THT]
  R7 = Resistor [tolerance=±5% resistance=2.2k package=THT]
  ContOne-Q = Arcade Button (white)
  ContOne-S = Round Pushbutton
  R8 = Resistor [tolerance=±5% resistance=330 package=THT]
  R9 = Resistor [tolerance=±5% resistance=2.2k package=THT]
  ContTwo-B = Arcade Button (white)
  ContTwo-S = Round Pushbutton
  R10 = Resistor [tolerance=±5% resistance=330 package=THT]
  R11 = Resistor [tolerance=±5% resistance=2.2k package=THT]
  ContThree-P = Arcade Button (white)
  ContThree-S = Round Pushbutton
  R12 = Resistor [tolerance=±5% resistance=330 package=THT]
  Main-Esc = Round Pushbutton
  Main-S = Round Pushbutton
  Main-R = Round Pushbutton
  Main-Q = Round Pushbutton
  Main-N = Round Pushbutton
  Main-Space = Round Pushbutton
  AB-B = Round Pushbutton
  AB-A = Round Pushbutton
  R15 = Resistor [tolerance=±5% resistance=2.2k package=THT]
  R16 = Resistor [tolerance=±5% resistance=330 package=THT]
  R17 = Resistor [tolerance=±5% resistance=680 package=THT]
  R18 = Resistor [tolerance=±5% resistance=1k package=THT]
  R19 = Resistor [tolerance=±5% resistance=3.3k package=THT]
  R20 = Resistor [tolerance=±5% resistance=4.7k package=THT]
  R13 = Resistor [tolerance=±5% resistance=2.2k package=THT]
  R14 = Resistor [tolerance=±5% resistance=330 package=THT]

nets:
  N1: ArduinoMicro.GND, R1.Pin_0, R2.Pin_0, OnethruFour-1.leg1, OnethruFour-2.leg1, OnethruFour-3.leg1, OnethruFour-4.leg1, ContOne-Q.no_name_yet#1, ContOne-S.leg1, ContTwo-B.no_name_yet#1, ContTwo-S.leg1, ContThree-P.no_name_yet#1, ContThree-S.leg1, Main-Esc.leg1, Main-S.leg1, Main-R.leg1, Main-Q.leg1, Main-N.leg1, Main-Space.leg1, AB-B.leg0, AB-A.leg0
  N2: ArduinoMicro.D2/SDA, LED1.anode
  N3: ArduinoMicro.D3/SCL, SW-KB-DISABLE.L2, R2.Pin_1
  N4: ArduinoMicro.5V, SW-KB-DISABLE.COM, R3.Pin_0, R7.Pin_1, R9.Pin_1, R11.Pin_1, R15.Pin_0, R13.Pin_0
  N5: ArduinoMicro.A5, OnethruFour-1.leg0, R3.Pin_1, R4.Pin_0
  N6: ArduinoMicro.A4, Main-Esc.leg0, R15.Pin_1, R16.Pin_0
  N7: ArduinoMicro.A3, AB-B.leg1, R13.Pin_1, R14.Pin_0
  N8: ArduinoMicro.A2, R11.Pin_0, ContThree-P.no_name_yet#2, R12.Pin_0
  N9: ArduinoMicro.A1, R9.Pin_0, ContTwo-B.no_name_yet#2, R10.Pin_0
  N10: ArduinoMicro.A0, R7.Pin_0, ContOne-Q.no_name_yet#2, R8.Pin_0
  N11: R1.Pin_1, LED1.cathode
  N12: OnethruFour-2.leg0, R4.Pin_1, R5.Pin_0
  N13: OnethruFour-3.leg0, R5.Pin_1, R6.Pin_0
  N14: OnethruFour-4.leg0, R6.Pin_1
  N15: ContOne-S.leg0, R8.Pin_1
  N16: ContTwo-S.leg0, R10.Pin_1
  N17: ContThree-S.leg0, R12.Pin_1
  N18: Main-S.leg0, R16.Pin_1, R17.Pin_0
  N19: Main-R.leg0, R17.Pin_1, R18.Pin_0
  N20: Main-Q.leg0, R18.Pin_1, R19.Pin_0
  N21: Main-N.leg0, R19.Pin_1, R20.Pin_0
  N22: Main-Space.leg0, R20.Pin_1
  N23: AB-A.leg1, R14.Pin_1

notes:
  YDKJ Box
  -BPM 2016.11
  Breakout board simulates RJ11 telephone cables and connectors
  AB-B
  AB-A
  AB Group
  Main Group
  OneThruFour Group
  ContThree-P
  ContTwo-B
  ContOne-Q
  ContThree-S
  ContOne-S
  ContTwo-S
  Controller One
  Controller Two
  Controller Three
  OnethruFour-1
  OnethruFour-2
  OnethruFour-3
  OnethruFour-4
  Main-Esc
  Main-S
  Main-R
  Main-Q
  Main-N
  Main-Space

custom parts:
  Arcade Button (white): Adafruit Arcade Button (white)
