# Fritzing sketch one_through_four (saved by Fritzing 0.9.3b)
breadboards: 2
stripboards: 6

parts:
  ArduinoMicro = Arduino Micro (Rev3)  # not connected
  R1 = Resistor [tolerance=±5% resistance=1k package=THT]
  LED1 = LED - 5mm [color="Red (633nm)" package="5 mm [THT]"]
  S1 = Toggle Switch [package=THT]
  R2 = Resistor [tolerance=±5% resistance=220 package=THT]
  BoxButton-1 = Square Pushbutton
  BoxButton-2 = Square Pushbutton
  BoxButton-3 = Square Pushbutton
  BoxButton-4 = Square Pushbutton
  R3 = Resistor [tolerance=±5% resistance=2.2k package=THT]
  R4 = Resistor [tolerance=±5% resistance=330 package=THT]
  R5 = Resistor [tolerance=±5% resistance=680 package=THT]
  R6 = Resistor [tolerance=±5% resistance=1k package=THT]
  PlayerButton-Qs = Round Pushbutton
  PlayerButton-Q = Arcade Button (white)
  R10 = Resistor [tolerance=±5% resistance=2.2k package=THT]
  R11 = Resistor [tolerance=±5% resistance=330 package=THT]
  R12 = Resistor [tolerance=±5% resistance=680 package=THT]
  R13 = Resistor [tolerance=±5% resistance=1k package=THT]
  R14 = Resistor [tolerance=±5% resistance=3.3k package=THT]
  R15 = Resistor [tolerance=±5% resistance=4.7k package=THT]
  PlayerButton-B = Arcade Button (white)
  PlayerButton-Bs = Round Pushbutton
  PlayerButton-P = Arcade Button (white)
  PlayerButton-Ps = Round Pushbutton

nets:
  N1: R1.Pin_0, R2.Pin_0, BoxButton-1.leg1, BoxButton-2.leg1, BoxButton-3.leg1, BoxButton-4.leg1, PlayerButton-Qs.leg0, PlayerButton-Q.no_name_yet#1, PlayerButton-B.no_name_yet#1, PlayerButton-Bs.leg0, PlayerButton-P.no_name_yet#1, PlayerButton-Ps.leg0
  N2: R1.Pin_1, LED1.cathode
  N3: S1.COM, R3.Pin_0, R10.Pin_0
  N4: S1.L2, R2.Pin_1
  N5: BoxButton-1.leg0, R3.Pin_1, R4.Pin_0
  N6: BoxButton-2.leg0, R4.Pin_1, R5.Pin_0
  N7: BoxButton-3.leg0, R5.Pin_1, R6.Pin_0
  N8: BoxButton-4.leg0, R6.Pin_1
  N9: PlayerButton-Qs.leg1, R11.Pin_1, R12.Pin_0
  N10: PlayerButton-Q.no_name_yet#2, R10.Pin_1, R11.Pin_0
  N11: R12.Pin_1, R13.Pin_0, PlayerButton-B.no_name_yet#2
  N12: R13.Pin_1, R14.Pin_0, PlayerButton-Bs.leg1
  N13: R14.Pin_1, R15.Pin_0, PlayerButton-P.no_name_yet#2
  N14: R15.Pin_1, PlayerButton-Ps.leg1

custom parts:
  Arcade Button (white): Adafruit Arcade Button (white)
